// Digital circuit 4-bit_PC.dig as structural Verilog
module _4_bit_PC (
  input  [3:0] I_3_0,
  input  CLK,
  output [3:0] O_3_0
);

  _1_bit_Reg _1_bit_reg_1 (.Din(I_3_0[3]), .Sel(1'b1), .CLK(CLK), .Dout(O_3_0[3]));
  _1_bit_Reg _1_bit_reg_2 (.Din(I_3_0[2]), .Sel(1'b1), .CLK(CLK), .Dout(O_3_0[2]));
  _1_bit_Reg _1_bit_reg_3 (.Din(I_3_0[1]), .Sel(1'b1), .CLK(CLK), .Dout(O_3_0[1]));
  _1_bit_Reg _1_bit_reg_4 (.Din(I_3_0[0]), .Sel(1'b1), .CLK(CLK), .Dout(O_3_0[0]));

  // Other names for the same wires on the sheet: A0 = I_3_0[0]; A1 = I_3_0[1]; A2 = I_3_0[2]; A3 = I_3_0[3];
  //   o0 = O_3_0[0]; o1 = O_3_0[1]; o2 = O_3_0[2]; o3 = O_3_0[3]
endmodule
