// Digital circuit 4-bit_Reg.dig as structural Verilog
module _4_bit_Reg (
  input  [3:0] Din_3_0,
  input  Sel,
  input  CLK,
  output [3:0] Dout_3_0
);

  _1_bit_Reg _1_bit_reg_1 (.Din(Din_3_0[3]), .Sel(Sel), .CLK(CLK), .Dout(Dout_3_0[3]));
  _1_bit_Reg _1_bit_reg_2 (.Din(Din_3_0[2]), .Sel(Sel), .CLK(CLK), .Dout(Dout_3_0[2]));
  _1_bit_Reg _1_bit_reg_3 (.Din(Din_3_0[1]), .Sel(Sel), .CLK(CLK), .Dout(Dout_3_0[1]));
  _1_bit_Reg _1_bit_reg_4 (.Din(Din_3_0[0]), .Sel(Sel), .CLK(CLK), .Dout(Dout_3_0[0]));

  // Other names for the same wires on the sheet: A0 = Din_3_0[0]; A1 = Din_3_0[1]; A2 = Din_3_0[2]; A3 = Din_3_0[3];
  //   o0 = Dout_3_0[0]; o1 = Dout_3_0[1]; o2 = Dout_3_0[2]; o3 = Dout_3_0[3]
endmodule
