// Digital circuit 5-bit_ALU.dig as structural Verilog
module _5_bit_ALU (
  input  [4:0] A_4_0,
  input  [4:0] B_4_0,
  input  [1:0] op_1_0,
  output [4:0] R_4_0,
  output CF
);

  wire [4:0] _5_bit_adder_1_r_4_0, _5_bit_shl_1_o_4_0, _5_bit_xor_1_o_4_0;

  _5_bit_xor _5_bit_xor_1 (.A_4_0(A_4_0), .B_4_0(B_4_0), .o_4_0(_5_bit_xor_1_o_4_0));
  _5_bit_adder _5_bit_adder_1 (.A_4_0(A_4_0), .B_4_0(B_4_0), .R_4_0(_5_bit_adder_1_r_4_0), .Cout(CF));
  _5_bit_SHL _5_bit_shl_1 (.A_4_0(A_4_0), .B_4_0(B_4_0), .o_4_0(_5_bit_shl_1_o_4_0));
  Multiplexer #(.Selector_Bits(2), .Bits(5)) multiplexer_1 (
    .sel(op_1_0), .in_0(_5_bit_xor_1_o_4_0), .in_1(_5_bit_adder_1_r_4_0), .in_2(_5_bit_shl_1_o_4_0),
    .in_3({5{1'b0}}), .out(R_4_0));
endmodule
