// Digital circuit 5-bit_CPU.dig as structural Verilog
module _5_bit_CPU (
  input  [3:0] WR_3_0,
  input  [15:0] WRD_15_0,
  input  WE,
  input  CLK,
  input  PC_EN,
  input  [3:0] RA2_3_0,
  output [15:0] RD2_15_0,
  output [2:0] R1_2_0,
  output [2:0] R2_2_0,
  output [2:0] WR_2_0,
  output [4:0] R_4_0,
  output [4:0] A_4_0,
  output [4:0] B_4_0,
  output [4:0] RR2_4_0
);

  wire _5_bit_alu_1_cf, CF, CPU_CLK, Imm_Sel, JMP_Sel, REG_EN;
  wire [1:0] OP;
  wire [3:0] _4_bit_pc_1_o_3_0, _4_bit_pc_adder_1_o_3_0, multiplexer_1_out;
  wire [4:0] _5_bit_reg_set_1_b_4_0;
  wire [15:0] _10x16ram_1_rd1_15_0;

  Multiplexer #(.Bits(4)) multiplexer_1 (
    .sel(JMP_Sel), .in_0(_4_bit_pc_adder_1_o_3_0), .in_1({R2_2_0[1:0], RR2_4_0[1:0]}), .out(multiplexer_1_out));
  _4_bit_PC_Adder _4_bit_pc_adder_1 (.I_3_0(_4_bit_pc_1_o_3_0), .O_3_0(_4_bit_pc_adder_1_o_3_0));
  _4_bit_PC _4_bit_pc_1 (.I_3_0(multiplexer_1_out), .CLK(CPU_CLK), .O_3_0(_4_bit_pc_1_o_3_0));
  and and_1 (CPU_CLK, PC_EN, CLK);
  _10x16RAM _10x16ram_1 (
    .RA1_3_0(_4_bit_pc_1_o_3_0), .RA2_3_0(RA2_3_0), .WR_3_0(WR_3_0), .WRD_15_0(WRD_15_0), .WE(WE), .CLK(CLK),
    .RD1_15_0({_10x16ram_1_rd1_15_0[15:12], R1_2_0, R2_2_0, RR2_4_0[1:0], _10x16ram_1_rd1_15_0[3:0]}),
    .RD2_15_0(RD2_15_0));
  _5_bit_Reg_set _5_bit_reg_set_1 (
    .WR_2_0(R1_2_0), .CLK(CPU_CLK), .WE(REG_EN), .WRD_4_0(R_4_0), .RA_2_0(R1_2_0), .RB_2_0(R2_2_0),
    .A_4_0(A_4_0), .B_4_0(_5_bit_reg_set_1_b_4_0));
  _5_bit_ALU _5_bit_alu_1 (.A_4_0(A_4_0), .B_4_0(B_4_0), .R_4_0(R_4_0), .op_1_0(OP), .CF(_5_bit_alu_1_cf));
  Flag_Reg flag_reg_1 (.CF_i(_5_bit_alu_1_cf), .CF(CF), .CLK(CPU_CLK));
  _5_bit_CU _5_bit_cu_1 (
    .Opcode_3_0(_10x16ram_1_rd1_15_0[15:12]), .CF(CF), .Op_1_0(OP), .REG_EN(REG_EN), .Imm_Sel(Imm_Sel),
    .JMP_Sel(JMP_Sel));
  Multiplexer #(.Bits(5)) multiplexer_2 (
    .sel(Imm_Sel), .in_0(_5_bit_reg_set_1_b_4_0), .in_1({R2_2_0, RR2_4_0[1:0]}), .out(B_4_0));

  assign RR2_4_0[4:2] = R2_2_0;
  assign WR_2_0 = R1_2_0;

  // Other names for the same wires on the sheet: RR2[4:0] = {R2_2_0, RR2_4_0[1:0]}; R2[2:0] = R2_2_0;
  //   R1[2:0] = R1_2_0; A[4:0] = A_4_0; B[4:0] = B_4_0; R[4:0] = R_4_0; RD2[15:0] = RD2_15_0

  // Notes on the sheet:
  //   Register mode: (Type of OP=00)+2bit(Type of operations)+3bit(Reg1)+3bit(Reg2)+6bit(Don't care)
  //   Immediate mode: (Type of OP=01)+2bit(Type of operations)+3bit(Reg1)+5bit(Imm. value)+4bit(Don't care)
  //   Branching mode:  (Type of OP=10)+1bit(Type of operations)+4bit(JMP Address)+9bit(Don't Care)
  //   XOR(OP=00) ADD(OP=01) SHL(OP=10) JMP(OP=00) JNC(op=01)
  //   XOR R1, R1(0000001001000000)
  //   ADD R1,5(0101001001010000)
endmodule
