// Digital circuit 5-bit_Reg_set.dig as structural Verilog
module _5_bit_Reg_set (
  input  [2:0] WR_2_0,
  input  WE,
  input  [4:0] WRD_4_0,
  input  CLK,
  input  [2:0] RA_2_0,
  input  [2:0] RB_2_0,
  output [4:0] A_4_0,
  output [4:0] B_4_0
);

  wire A0, A1, A2, A3, A4, D0, D1, D2, D3, D4, decoder_1_out_5;
  wire [4:0] R0, R1, R2, R3, R4;

  Decoder #(.Selector_Bits(3)) decoder_1 (
    .sel(WR_2_0), .out_0(A0), .out_1(A1), .out_2(A2), .out_3(A3), .out_4(A4), .out_5(decoder_1_out_5),
    .out_6(decoder_1_out_5), .out_7(decoder_1_out_5));
  and and_1 (D0, A0, WE);
  and and_2 (D2, A2, WE);
  _5_bit_Reg _5_bit_reg_1 (.Din_4_0(WRD_4_0), .Sel(D4), .CLK(CLK), .Dout_4_0(R4));
  _5_bit_Reg _5_bit_reg_2 (.Din_4_0(WRD_4_0), .Sel(D3), .CLK(CLK), .Dout_4_0(R3));
  _5_bit_Reg _5_bit_reg_3 (.Din_4_0(WRD_4_0), .Sel(D2), .CLK(CLK), .Dout_4_0(R2));
  _5_bit_Reg _5_bit_reg_4 (.Din_4_0(WRD_4_0), .Sel(D1), .CLK(CLK), .Dout_4_0(R1));
  _5_bit_Reg _5_bit_reg_5 (.Din_4_0(WRD_4_0), .Sel(D0), .CLK(CLK), .Dout_4_0(R0));
  and and_3 (D1, A1, WE);
  and and_4 (D3, A3, WE);
  Multiplexer #(.Bits(5), .Selector_Bits(3)) multiplexer_1 (
    .sel(RA_2_0), .in_0(R0), .in_1(R1), .in_2(R2), .in_3(R3), .in_4(R4), .in_5({5{1'b0}}), .in_6({5{1'b0}}),
    .in_7({5{1'b0}}), .out(A_4_0));
  Multiplexer #(.Selector_Bits(3), .Bits(5)) multiplexer_2 (
    .sel(RB_2_0), .in_0(R0), .in_1(R1), .in_2(R2), .in_3(R3), .in_4(R4), .in_5({5{1'b0}}), .in_6({5{1'b0}}),
    .in_7({5{1'b0}}), .out(B_4_0));
  and and_5 (D4, A4, WE);
  // also tied to GND on the sheet: decoder_1_out_5

  // Other names for the same wires on the sheet: WRD[4:0] = WRD_4_0
endmodule
