// Digital circuit 5-bit_SHL.dig as structural Verilog
module _5_bit_SHL (
  input  [4:0] A_4_0,
  input  [4:0] B_4_0,
  output [4:0] o_4_0
);

  Multiplexer #(.Selector_Bits(3)) multiplexer_1 (
    .sel(B_4_0[2:0]), .in_0(A_4_0[4]), .in_1(A_4_0[3]), .in_2(A_4_0[2]), .in_3(A_4_0[1]), .in_4(A_4_0[0]),
    .in_5(1'b0), .in_6(1'b0), .in_7(1'b0), .out(o_4_0[4]));
  Multiplexer #(.Selector_Bits(3)) multiplexer_2 (
    .sel(B_4_0[2:0]), .in_0(A_4_0[3]), .in_1(A_4_0[2]), .in_2(A_4_0[1]), .in_3(A_4_0[0]), .in_4(1'b0),
    .in_5(1'b0), .in_6(1'b0), .in_7(1'b0), .out(o_4_0[3]));
  Multiplexer #(.Selector_Bits(3)) multiplexer_3 (
    .sel(B_4_0[2:0]), .in_0(A_4_0[2]), .in_1(A_4_0[1]), .in_2(A_4_0[0]), .in_3(1'b0), .in_4(1'b0),
    .in_5(1'b0), .in_6(1'b0), .in_7(1'b0), .out(o_4_0[2]));
  Multiplexer #(.Selector_Bits(3)) multiplexer_4 (
    .sel(B_4_0[2:0]), .in_0(A_4_0[1]), .in_1(A_4_0[0]), .in_2(1'b0), .in_3(1'b0), .in_4(1'b0), .in_5(1'b0),
    .in_6(1'b0), .in_7(1'b0), .out(o_4_0[1]));
  Multiplexer #(.Selector_Bits(3)) multiplexer_5 (
    .sel(B_4_0[2:0]), .in_0(A_4_0[0]), .in_1(1'b0), .in_2(1'b0), .in_3(1'b0), .in_4(1'b0), .in_5(1'b0),
    .in_6(1'b0), .in_7(1'b0), .out(o_4_0[0]));

  assign B_4_0[3] = B_4_0[4];
  // also tied to GND on the sheet: B_4_0[4]

  // Other names for the same wires on the sheet: A0 = A_4_0[0]; A1 = A_4_0[1]; A2 = A_4_0[2]; A3 = A_4_0[3];
  //   A4 = A_4_0[4]; B0 = B_4_0[0]; B1 = B_4_0[1]; B2 = B_4_0[2]; o0 = o_4_0[0]; o1 = o_4_0[1]; o2 = o_4_0[2];
  //   o3 = o_4_0[3]; o4 = o_4_0[4]
endmodule
