// Digital circuit 5-bit_adder.dig as structural Verilog
module _5_bit_adder (
  input  [4:0] A_4_0,
  input  [4:0] B_4_0,
  output [4:0] R_4_0,
  output Cout
);

  wire fa_2_cout, fa_3_cout, fa_4_cout, fa_5_cout;

  FA fa_1 (.y(B_4_0[4]), .x(A_4_0[4]), .cin(fa_2_cout), .s(R_4_0[4]), .cout(Cout));
  FA fa_2 (.y(B_4_0[3]), .x(A_4_0[3]), .cin(fa_3_cout), .s(R_4_0[3]), .cout(fa_2_cout));
  FA fa_3 (.y(B_4_0[2]), .x(A_4_0[2]), .cin(fa_4_cout), .s(R_4_0[2]), .cout(fa_3_cout));
  FA fa_4 (.y(B_4_0[1]), .x(A_4_0[1]), .cin(fa_5_cout), .s(R_4_0[1]), .cout(fa_4_cout));
  FA fa_5 (.y(B_4_0[0]), .x(A_4_0[0]), .cin(1'b0), .s(R_4_0[0]), .cout(fa_5_cout));
endmodule
