// Digital circuit 5-bit_xor.dig as structural Verilog
module _5_bit_xor (
  input  [4:0] A_4_0,
  input  [4:0] B_4_0,
  output [4:0] o_4_0
);

  xor xor_1 (o_4_0[0], A_4_0[0], B_4_0[0]);
  xor xor_2 (o_4_0[1], A_4_0[1], B_4_0[1]);
  xor xor_3 (o_4_0[2], A_4_0[2], B_4_0[2]);
  xor xor_4 (o_4_0[3], A_4_0[3], B_4_0[3]);
  xor xor_5 (o_4_0[4], A_4_0[4], B_4_0[4]);

  // Other names for the same wires on the sheet: A0 = A_4_0[0]; A1 = A_4_0[1]; A2 = A_4_0[2]; A3 = A_4_0[3];
  //   A4 = A_4_0[4]; B0 = B_4_0[0]; B1 = B_4_0[1]; B2 = B_4_0[2]; B3 = B_4_0[3]; B4 = B_4_0[4]; o0 = o_4_0[0];
  //   o1 = o_4_0[1]; o2 = o_4_0[2]; o3 = o_4_0[3]; o4 = o_4_0[4]
endmodule
