// Digital circuit FA.dig as structural Verilog
module FA (
  input  x,
  input  y,
  input  cin,
  output s,
  output cout
);

  wire and_1_out, and_2_out, xor_1_out;

  xor xor_1 (xor_1_out, x, y);
  and and_1 (and_1_out, x, y);
  xor xor_2 (s, xor_1_out, cin);
  and and_2 (and_2_out, xor_1_out, cin);
  or or_1 (cout, and_2_out, and_1_out);
endmodule
