// Digital circuit Flag_Reg.dig as structural Verilog
module Flag_Reg (
  input  CF_i,
  input  CLK,
  output CF
);

  _1_bit_Reg _1_bit_reg_1 (.Din(CF_i), .Sel(1'b1), .CLK(CLK), .Dout(CF));
endmodule
